// Logisim project 8 Bit CPU Design.circ as structural Verilog: 16 circuits, main circuit main
module main (
  input  [7:0] Testing_Data,
  input  OE,
  input  OE_testing_data,
  input  [3:0] OE_testing_data_2,
  input  in_5,
  input  in_6,
  input  [2:0] in_7,
  output [3:0] MAR_content,
  output [3:0] Content_of_Counter,
  output [7:0] IR_Content,
  output [7:0] MBR_content,
  output [7:0] Register_A_content,
  output [7:0] ALU_content,
  output [2:0] Content_of_Counter_2,
  output [7:0] out_15,
  output [7:0] Register_B_content
);

  wire clock_out, Control_unit_1_c0, Control_unit_1_c1, Control_unit_1_c2, Control_unit_1_c3,
       Control_unit_1_c4, Control_unit_1_c5, Control_unit_1_c6, Control_unit_1_c7, Control_unit_1_c8,
       Control_unit_1_c9, Control_unit_1_c10, Control_unit_1_c11, Control_unit_2_c12, Control_unit_2_c13,
       Control_unit_2_c14, Control_unit_2_c15;
  wire [3:0] bitselector_2_out, controlled_buffer_1_out, MAR_dout;
  wire [7:0] alu_1_dout, bit_extender_1_out, bit_extender_2_out, register_1_dout;
  wire [31:0] Decimal_Decoder_2_out_2, Decimal_Decoder_3_out_2, Decimal_Decoder_4_out_2,
       Decimal_Decoder_5_out_2, Decimal_Decoder_out_2;

  Clock clock (.out(clock_out));
  Counter #(.width(4), .max('h3)) program_counter (
    .D(controlled_buffer_1_out), .count(Control_unit_1_c1), .Q(Content_of_Counter), .clk(clock_out));  // open: load, carry, clr
  Register register_1 (
    .clock(clock_out), .WE(Control_unit_1_c7), .Din(alu_1_dout), .OE(Control_unit_1_c8),
    .Dout(register_1_dout), .Stored_Data(IR_Content));
  Register register_2 (
    .clock(clock_out), .WE(Control_unit_2_c12), .Din(alu_1_dout), .Stored_Data(Register_A_content));  // open: OE, Dout
  ALU alu_1 (
    .Carry(in_5), .Register_A(Register_A_content), .Register_B(Register_B_content), .selection_key(in_7),
    .Dout(alu_1_dout), .OE(Control_unit_1_c11), .ALU_result(ALU_content), .WEDivision(in_6));  // open: in_7, out_8, out_10
  Register register_3 (
    .clock(clock_out), .WE(Control_unit_2_c13), .Din(alu_1_dout), .Stored_Data(Register_B_content));  // open: OE, Dout
  assign controlled_buffer_1_out = Control_unit_1_c0 ? Content_of_Counter : 4'bz;  // Controlled_Buffer controlled_buffer_1
  Decimal_Decoder Decimal_Decoder (.Din(Register_A_content), .out_2(Decimal_Decoder_out_2));
  Decimal_Decoder Decimal_Decoder_2 (.Din(Register_B_content), .out_2(Decimal_Decoder_2_out_2));
  Decimal_Decoder Decimal_Decoder_3 (.Din(bit_extender_1_out), .out_2(Decimal_Decoder_3_out_2));
  assign bit_extender_1_out = {{4{1'b0}}, Content_of_Counter};  // Bit_Extender bit_extender_1
  _7_Segment_Display u_7_segment_display_1 (
    .g(Decimal_Decoder_out_2[15]), .f(Decimal_Decoder_out_2[14]), .a(Decimal_Decoder_out_2[13]),
    .b(Decimal_Decoder_out_2[12]), .e(Decimal_Decoder_out_2[31]), .d(Decimal_Decoder_out_2[30]),
    .c(Decimal_Decoder_out_2[29]), .dp(Decimal_Decoder_out_2[28]));
  _7_Segment_Display u_7_segment_display_2 (
    .g(Decimal_Decoder_2_out_2[15]), .f(Decimal_Decoder_2_out_2[14]), .a(Decimal_Decoder_2_out_2[13]),
    .b(Decimal_Decoder_2_out_2[12]), .e(Decimal_Decoder_2_out_2[31]), .d(Decimal_Decoder_2_out_2[30]),
    .c(Decimal_Decoder_2_out_2[29]), .dp(Decimal_Decoder_2_out_2[28]));
  _7_Segment_Display u_7_segment_display_3 (
    .g(Decimal_Decoder_2_out_2[11]), .f(Decimal_Decoder_2_out_2[10]), .a(Decimal_Decoder_2_out_2[9]),
    .b(Decimal_Decoder_2_out_2[8]), .e(Decimal_Decoder_2_out_2[27]), .d(Decimal_Decoder_2_out_2[26]),
    .c(Decimal_Decoder_2_out_2[25]), .dp(Decimal_Decoder_2_out_2[24]));
  _7_Segment_Display u_7_segment_display_4 (
    .g(Decimal_Decoder_3_out_2[3]), .f(Decimal_Decoder_3_out_2[2]), .a(Decimal_Decoder_3_out_2[1]),
    .b(Decimal_Decoder_3_out_2[0]), .e(Decimal_Decoder_3_out_2[19]), .d(Decimal_Decoder_3_out_2[18]),
    .c(Decimal_Decoder_3_out_2[17]), .dp(Decimal_Decoder_3_out_2[16]));
  _7_Segment_Display u_7_segment_display_5 (
    .g(Decimal_Decoder_out_2[11]), .f(Decimal_Decoder_out_2[10]), .a(Decimal_Decoder_out_2[9]),
    .b(Decimal_Decoder_out_2[8]), .e(Decimal_Decoder_out_2[27]), .d(Decimal_Decoder_out_2[26]),
    .c(Decimal_Decoder_out_2[25]), .dp(Decimal_Decoder_out_2[24]));
  _7_Segment_Display u_7_segment_display_6 (
    .g(Decimal_Decoder_out_2[7]), .f(Decimal_Decoder_out_2[6]), .a(Decimal_Decoder_out_2[5]),
    .b(Decimal_Decoder_out_2[4]), .e(Decimal_Decoder_out_2[23]), .d(Decimal_Decoder_out_2[22]),
    .c(Decimal_Decoder_out_2[21]), .dp(Decimal_Decoder_out_2[20]));
  _7_Segment_Display u_7_segment_display_7 (
    .g(Decimal_Decoder_2_out_2[7]), .f(Decimal_Decoder_2_out_2[6]), .a(Decimal_Decoder_2_out_2[5]),
    .b(Decimal_Decoder_2_out_2[4]), .e(Decimal_Decoder_2_out_2[23]), .d(Decimal_Decoder_2_out_2[22]),
    .c(Decimal_Decoder_2_out_2[21]), .dp(Decimal_Decoder_2_out_2[20]));
  _7_Segment_Display u_7_segment_display_8 (
    .g(Decimal_Decoder_2_out_2[3]), .f(Decimal_Decoder_2_out_2[2]), .a(Decimal_Decoder_2_out_2[1]),
    .b(Decimal_Decoder_2_out_2[0]), .e(Decimal_Decoder_2_out_2[19]), .d(Decimal_Decoder_2_out_2[18]),
    .c(Decimal_Decoder_2_out_2[17]), .dp(Decimal_Decoder_2_out_2[16]));
  _7_Segment_Display u_7_segment_display_9 (
    .g(Decimal_Decoder_out_2[3]), .f(Decimal_Decoder_out_2[2]), .a(Decimal_Decoder_out_2[1]),
    .b(Decimal_Decoder_out_2[0]), .e(Decimal_Decoder_out_2[19]), .d(Decimal_Decoder_out_2[18]),
    .c(Decimal_Decoder_out_2[17]), .dp(Decimal_Decoder_out_2[16]));
  BitSelector #(.group(4)) bitselector_1 (.in(register_1_dout), .out(controlled_buffer_1_out), .sel(1'b0));
  LED D6 (.in(alu_1_dout[6]));
  LED D5 (.in(alu_1_dout[5]));
  LED D4 (.in(alu_1_dout[4]));
  LED D7 (.in(alu_1_dout[7]));
  assign alu_1_dout = OE_testing_data ? Testing_Data : 8'bz;  // Controlled_Buffer controlled_buffer_2
  LED D1 (.in(alu_1_dout[1]));
  LED D3 (.in(alu_1_dout[3]));
  LED D0 (.in(alu_1_dout[0]));
  LED D2 (.in(alu_1_dout[2]));
  MAR MAR (
    .clock(clock_out), .WE(Control_unit_1_c9), .Din(controlled_buffer_1_out), .OE(Control_unit_1_c10),
    .Dout(MAR_dout), .Stored_Data(MAR_content));
  assign alu_1_dout = Control_unit_1_c5 ? MBR_content : 8'bz;  // Controlled_Buffer controlled_buffer_3
  Register MBR (
    .clock(clock_out), .WE(Control_unit_1_c4), .Din(alu_1_dout), .OE(Control_unit_1_c6), .Dout(alu_1_dout),
    .Stored_Data(MBR_content));
  Register output_register (
    .clock(clock_out), .WE(Control_unit_2_c15), .Din(alu_1_dout), .OE(Control_unit_2_c14), .Dout(alu_1_dout),
    .Stored_Data(out_15));
  Decimal_Decoder Decimal_Decoder_4 (.Din(out_15), .out_2(Decimal_Decoder_4_out_2));
  assign MAR_dout = OE ? OE_testing_data_2 : 4'bz;  // Controlled_Buffer controlled_buffer_4
  _7_Segment_Display u_7_segment_display_10 (
    .g(Decimal_Decoder_4_out_2[15]), .f(Decimal_Decoder_4_out_2[14]), .a(Decimal_Decoder_4_out_2[13]),
    .b(Decimal_Decoder_4_out_2[12]), .e(Decimal_Decoder_4_out_2[31]), .d(Decimal_Decoder_4_out_2[30]),
    .c(Decimal_Decoder_4_out_2[29]), .dp(Decimal_Decoder_4_out_2[28]));
  _7_Segment_Display u_7_segment_display_11 (
    .g(Decimal_Decoder_4_out_2[11]), .f(Decimal_Decoder_4_out_2[10]), .a(Decimal_Decoder_4_out_2[9]),
    .b(Decimal_Decoder_4_out_2[8]), .e(Decimal_Decoder_4_out_2[27]), .d(Decimal_Decoder_4_out_2[26]),
    .c(Decimal_Decoder_4_out_2[25]), .dp(Decimal_Decoder_4_out_2[24]));
  _7_Segment_Display u_7_segment_display_12 (
    .g(Decimal_Decoder_4_out_2[7]), .f(Decimal_Decoder_4_out_2[6]), .a(Decimal_Decoder_4_out_2[5]),
    .b(Decimal_Decoder_4_out_2[4]), .e(Decimal_Decoder_4_out_2[23]), .d(Decimal_Decoder_4_out_2[22]),
    .c(Decimal_Decoder_4_out_2[21]), .dp(Decimal_Decoder_4_out_2[20]));
  _7_Segment_Display u_7_segment_display_13 (
    .g(Decimal_Decoder_4_out_2[3]), .f(Decimal_Decoder_4_out_2[2]), .a(Decimal_Decoder_4_out_2[1]),
    .b(Decimal_Decoder_4_out_2[0]), .e(Decimal_Decoder_4_out_2[19]), .d(Decimal_Decoder_4_out_2[18]),
    .c(Decimal_Decoder_4_out_2[17]), .dp(Decimal_Decoder_4_out_2[16]));
  LED D7_2 (.in(alu_1_dout[7]));
  LED D6_2 (.in(alu_1_dout[6]));
  LED D2_2 (.in(alu_1_dout[2]));
  LED D4_2 (.in(alu_1_dout[4]));
  LED D3_2 (.in(alu_1_dout[3]));
  LED D5_2 (.in(alu_1_dout[5]));
  LED D1_2 (.in(alu_1_dout[1]));
  LED D0_2 (.in(alu_1_dout[0]));
  RAM #(.addrWidth(4), .bus("separate")) ram_1 (
    .addr(MAR_dout), .din(alu_1_dout), .data(alu_1_dout), .str(Control_unit_1_c2), .clk(clock_out),
    .ld(Control_unit_1_c3));  // open: sel, clr
  BitSelector #(.group(4)) bitselector_2 (.in(IR_Content), .out(bitselector_2_out), .sel(1'b1));
  Counter #(.width(3), .max('h5)) Step_counter (
    .Q(Content_of_Counter_2), .clk(clock_out));  // open: load, D, count, carry, clr
  assign bit_extender_2_out = {{5{1'b0}}, Content_of_Counter_2};  // Bit_Extender bit_extender_2
  Control_Unit_1 Control_unit_1 (
    .OPC3(bitselector_2_out[3]), .OPC2(bitselector_2_out[2]), .OPC1(bitselector_2_out[1]),
    .OPC0(bitselector_2_out[0]), .SC2(Content_of_Counter_2[2]), .SC1(Content_of_Counter_2[1]),
    .SC0(Content_of_Counter_2[0]), .C0(Control_unit_1_c0), .C1(Control_unit_1_c1), .C2(Control_unit_1_c2),
    .C3(Control_unit_1_c3), .C4(Control_unit_1_c4), .C5(Control_unit_1_c5), .C6(Control_unit_1_c6),
    .C7(Control_unit_1_c7), .C8(Control_unit_1_c8), .C9(Control_unit_1_c9), .C10(Control_unit_1_c10),
    .C11(Control_unit_1_c11));
  Control_unit_2 Control_unit_2 (
    .OPC3(bitselector_2_out[3]), .OPC2(bitselector_2_out[2]), .OPC1(bitselector_2_out[1]),
    .OPC0(bitselector_2_out[0]), .SC2(Content_of_Counter_2[2]), .SC1(Content_of_Counter_2[1]),
    .SC0(Content_of_Counter_2[0]), .C12(Control_unit_2_c12), .C13(Control_unit_2_c13),
    .C14(Control_unit_2_c14), .C15(Control_unit_2_c15));
  Decimal_Decoder Decimal_Decoder_5 (.Din(bit_extender_2_out), .out_2(Decimal_Decoder_5_out_2));
  _7_Segment_Display u_7_segment_display_14 (
    .g(Decimal_Decoder_5_out_2[3]), .f(Decimal_Decoder_5_out_2[2]), .a(Decimal_Decoder_5_out_2[1]),
    .b(Decimal_Decoder_5_out_2[0]), .e(Decimal_Decoder_5_out_2[19]), .d(Decimal_Decoder_5_out_2[18]),
    .c(Decimal_Decoder_5_out_2[17]), .dp(Decimal_Decoder_5_out_2[16]));

  // Notes on the sheet:
  //   ALU
  //   program counter 
  //   Instructon Register
  //   Register A
  //   Register B
  //   Internal Address Bus (4Bits)
  //   Internal data bus
  //   External Address Bus
  //   External data bus
  //   Step counter 
  //   C15
  //   C14
  //   C13
  //   C12
  //   C11
  //   C10
  //   C9
  //   C8
  //   C7
  //   C6
  //   C5
  //   C4
  //   C3
  //   C2
  //   C1
  //   C0
endmodule

module Memory_cell (
  input  clock,
  input  WE,
  input  Din,
  input  OE,
  input  Reset,
  output Dout,
  output stored_data
);

  wire and_1_out, and_2_out, not_1_out, or_1_out;

  not not_1 (not_1_out, WE);
  and and_1 (and_1_out, stored_data, not_1_out);
  and and_2 (and_2_out, WE, Din);
  or or_1 (or_1_out, and_1_out, and_2_out);
  D_Flip_Flop d_ff_1 (.clk(clock), .D(or_1_out), .Q(stored_data), .reset(Reset));  // open: Qn, preset, en
  assign Dout = OE ? stored_data : 1'bz;  // Controlled_Buffer controlled_buffer_1

  // Notes on the sheet:
  //   Memory cell
endmodule

module Register (
  input  clock,
  input  WE,
  input  [7:0] Din,
  input  OE,
  output [7:0] Dout,
  output [7:0] Stored_Data
);

  Memory_cell _0 (
    .clock(clock), .WE(WE), .Din(Din[0]), .OE(OE), .Dout(Dout[0]), .stored_data(Stored_Data[0]));  // open: Reset
  Memory_cell _1 (
    .clock(clock), .WE(WE), .Din(Din[1]), .OE(OE), .Dout(Dout[1]), .stored_data(Stored_Data[1]));  // open: Reset
  Memory_cell _2 (
    .clock(clock), .WE(WE), .Din(Din[2]), .OE(OE), .Dout(Dout[2]), .stored_data(Stored_Data[2]));  // open: Reset
  Memory_cell _3 (
    .clock(clock), .WE(WE), .Din(Din[3]), .OE(OE), .Dout(Dout[3]), .stored_data(Stored_Data[3]));  // open: Reset
  Memory_cell _4 (
    .clock(clock), .WE(WE), .Din(Din[4]), .OE(OE), .Dout(Dout[4]), .stored_data(Stored_Data[4]));  // open: Reset
  Memory_cell _5 (
    .clock(clock), .WE(WE), .Din(Din[5]), .OE(OE), .Dout(Dout[5]), .stored_data(Stored_Data[5]));  // open: Reset
  Memory_cell _6 (
    .clock(clock), .WE(WE), .Din(Din[6]), .OE(OE), .Dout(Dout[6]), .stored_data(Stored_Data[6]));  // open: Reset
  Memory_cell _7 (
    .clock(clock), .WE(WE), .Din(Din[7]), .OE(OE), .Dout(Dout[7]), .stored_data(Stored_Data[7]));  // open: Reset

  // Notes on the sheet:
  //   8 Bit Register
endmodule

module MAR (
  input  clock,
  input  WE,
  input  [3:0] Din,
  input  OE,
  output [3:0] Dout,
  output [3:0] Stored_Data
);

  Memory_cell _0 (
    .clock(clock), .WE(WE), .Din(Din[0]), .OE(OE), .Dout(Dout[0]), .stored_data(Stored_Data[0]));  // open: Reset
  Memory_cell _1 (
    .clock(clock), .WE(WE), .Din(Din[1]), .OE(OE), .Dout(Dout[1]), .stored_data(Stored_Data[1]));  // open: Reset
  Memory_cell _2 (
    .clock(clock), .WE(WE), .Din(Din[2]), .OE(OE), .Dout(Dout[2]), .stored_data(Stored_Data[2]));  // open: Reset
  Memory_cell _3 (
    .clock(clock), .WE(WE), .Din(Din[3]), .OE(OE), .Dout(Dout[3]), .stored_data(Stored_Data[3]));  // open: Reset

  // Notes on the sheet:
  //   MAR
endmodule

module ALU (
  input  [7:0] Register_A,
  input  [7:0] Register_B,
  input  OE,
  input  Carry,
  input  [2:0] selection_key,
  input  WEDivision,
  input  in_7,
  output out_8,
  output [7:0] Dout,
  output out_10,
  output [7:0] ALU_result
);

  wire [7:0] adder_1_sum, bit_extender_1_out, n8x8divider_1_q, nand_1_out, nor_1_out, subtractor_1_d,
       xnor_1_out, xor_1_out;
  wire [15:0] n8x8multipier_1_out_11;

  Adder adder_1 (.SUM(adder_1_sum), .Cout(out_8), .in_1(1'b0), .B(Register_B), .A(Register_A));
  subtractor subtractor_1 (.A(Register_A), .B(Register_B), .D(subtractor_1_d), .Bout(out_10));
  _8x8Divider u_8x8divider_1 (.A(Register_A), .B(Register_B), .Q(n8x8divider_1_q), .k(WEDivision));
  assign xor_1_out = Register_B ^ Register_A;  // XOR_Gate xor_1, 8 bits wide
  assign nand_1_out = ~(Register_B & Register_A);  // NAND_Gate nand_1, 8 bits wide
  assign xnor_1_out = ~(Register_B ^ Register_A);  // XNOR_Gate xnor_1, 8 bits wide
  assign nor_1_out = ~(Register_B | Register_A);  // NOR_Gate nor_1, 8 bits wide
  assign bit_extender_1_out = {{7{1'b0}}, Carry};  // Bit_Extender bit_extender_1
  _8x8Multipier u_8x8multipier_1 (
    .A(Register_A), .B(Register_B), .in_3(bit_extender_1_out[7]), .in_10(bit_extender_1_out[6]),
    .in_9(bit_extender_1_out[5]), .in_8(bit_extender_1_out[4]), .in_7(bit_extender_1_out[3]),
    .in_6(bit_extender_1_out[2]), .in_5(bit_extender_1_out[1]), .in_4(bit_extender_1_out[0]),
    .out_11(n8x8multipier_1_out_11));
  Bit_Extender #(.out_width(1)) bit_extender_2 (.in(n8x8multipier_1_out_11[15:8]), .out(in_7));
  _8x3MUX u_8x3mux_1 (
    .d0(adder_1_sum), .d1(subtractor_1_d), .d2(n8x8multipier_1_out_11[7:0]), .d3(n8x8divider_1_q),
    .d4(xor_1_out), .d5(nand_1_out), .d6(xnor_1_out), .d7(nor_1_out), .in_9(selection_key), .out(ALU_result));
  assign Dout = OE ? ALU_result : 8'bz;  // Controlled_Buffer controlled_buffer_1

  // Notes on the sheet:
  //   000 - Addition
  //   oo1 - Subtract
  //   010 - Multiply 
  //   011 - Divide
  //   100 - XOR
  //   101 - NAND
  //   110 - XNOR
  //   111 - NOR
  //   Selection key 
endmodule

module Decimal_Decoder (
  input  [7:0] Din,
  output [31:0] out_2
);

  ROM #(.dataWidth(32)) rom_1 (
    .addr(Din),
    .data({out_2[31:28], out_2[15:12], out_2[27:24], out_2[11:8], out_2[23:20], out_2[7:4], out_2[19:16], out_2[3:0]}));  // open: sel

  // Notes on the sheet:
  //   Decimal Decoder
  //   contents of rom_1 (hex, n*v repeats v):
  //   e7 21 cb 6b 2d 6e ee 23 ef 2f 21e7 2121 21cb 216b 212d 216e 21ee 2123 21ef 212f cbe7 cb21 cbcb cb6b
  //   cb2d cb6e cbee cb23 cbef cb2f 6be7 6b21 6bcb 6b6b 6b2d 6b6e 6bee 6b23 6bef 6b2f 2de7 2d21 2dcb 2d6b
  //   2d2d 2d6e 2dee 2d23 2def 2d2f 6ee7 6e21 6ecb 6e6b 6e2d 6e6e 6eee 6e23 6eef 6e2f eee7 ee21 eecb ee6b
  //   ee2d ee6e eeee ee23 eeef ee2f 23e7 2321 23cb 236b 232d 236e 23ee 2323 23ef 232f efe7 ef21 efcb ef6b
  //   ef2d ef6e efee ef23 efef ef2f 2fe7 2f21 2fcb 2f6b 2f2d 2f6e 2fee 2f23 2fef 2f2f 21e7e7 21e721 21e7cb
  //   21e76b 21e72d 21e76e 21e7ee 21e723 21e7ef 21e72f 2121e7 212121 2121cb 21216b 21212d 21216e 2121ee
  //   212123 2121ef 21212f 21cbe7 21cb21 21cbcb 21cb6b 21cb2d 21cb6e 21cbee 21cb23 21cbef 21cb2f 216be7
  //   216b21 216bcb 216b6b 216b2d 216b6e 216bee 216b23 216bef 216b2f 212de7 212d21 212dcb 212d6b 212d2d
  //   212d6e 212dee 212d23 212def 212d2f 216ee7 216e21 216ecb 216e6b 216e2d 216e6e 216eee 216e23 216eef
  //   216e2f 21eee7 21ee21 21eecb 21ee6b 21ee2d 21ee6e 21eeee 21ee23 21eeef 21ee2f 2123e7 212321 2123cb
  //   21236b 21232d 21236e 2123ee 212323 2123ef 21232f 21efe7 21ef21 21efcb 21ef6b 21ef2d 21ef6e 21efee
  //   21ef23 21efef 21ef2f 212fe7 212f21 212fcb 212f6b 212f2d 212f6e 212fee 212f23 212fef 212f2f cbe7e7
  //   cbe721 cbe7cb cbe76b cbe72d cbe76e cbe7ee cbe723 cbe7ef cbe72f cb21e7 cb2121 cb21cb cb216b cb212d
  //   cb216e cb21ee cb2123 cb21ef cb212f cbcbe7 cbcb21 cbcbcb cbcb6b cbcb2d cbcb6e cbcbee cbcb23 cbcbef
  //   cbcb2f cb6be7 cb6b21 cb6bcb cb6b6b cb6b2d cb6b6e cb6bee cb6b23 cb6bef cb6b2f cb2de7 cb2d21 cb2dcb
  //   cb2d6b cb2d2d cb2d6e cb2dee cb2d23 cb2def cb2d2f cb6ee7 cb6e21 cb6ecb cb6e6b cb6e2d cb6e6e
endmodule

module Control_Unit_1 (
  input  OPC3,
  input  OPC2,
  input  OPC1,
  input  OPC0,
  input  SC2,
  input  SC1,
  input  SC0,
  output C0,
  output C1,
  output C2,
  output C3,
  output C4,
  output C5,
  output C6,
  output C7,
  output C8,
  output C9,
  output C10,
  output C11
);

  wire and_4_out, and_5_out, and_6_out, and_7_out, and_8_out, and_9_out, and_10_out, and_13_out, and_14_out,
       and_15_out, and_16_out, and_17_out, and_18_out, and_19_out, and_20_out, not_1_out, not_2_out,
       not_3_out, not_4_out, not_5_out, not_6_out, not_7_out, not_8_out, not_9_out, not_10_out, not_11_out,
       not_12_out, not_13_out, not_14_out, not_15_out, not_16_out, not_17_out, not_18_out, not_19_out,
       not_20_out, not_21_out, not_22_out, not_23_out, not_24_out, not_25_out, not_26_out, not_27_out,
       not_28_out, not_29_out, not_30_out, not_31_out, not_32_out, not_33_out, not_34_out, not_35_out,
       not_36_out, not_37_out, not_38_out, not_39_out, not_40_out, not_41_out, not_42_out, not_43_out,
       not_44_out;

  not not_1 (not_1_out, SC2);
  not not_2 (not_2_out, SC1);
  not not_3 (not_3_out, SC0);
  not not_4 (not_4_out, SC2);
  not not_5 (not_5_out, SC1);
  not not_6 (not_6_out, SC1);
  not not_7 (not_7_out, SC0);
  not not_8 (not_8_out, SC2);
  not not_9 (not_9_out, SC1);
  not not_10 (not_10_out, OPC1);
  not not_11 (not_11_out, SC1);
  not not_12 (not_12_out, SC0);
  not not_13 (not_13_out, SC2);
  not not_14 (not_14_out, SC1);
  not not_15 (not_15_out, OPC1);
  not not_16 (not_16_out, SC1);
  not not_17 (not_17_out, SC0);
  not not_18 (not_18_out, SC2);
  not not_19 (not_19_out, SC2);
  not not_20 (not_20_out, SC0);
  not not_21 (not_21_out, OPC1);
  not not_22 (not_22_out, SC1);
  not not_23 (not_23_out, SC1);
  not not_24 (not_24_out, SC0);
  not not_25 (not_25_out, SC2);
  not not_26 (not_26_out, SC0);
  not not_27 (not_27_out, OPC1);
  not not_28 (not_28_out, SC2);
  not not_29 (not_29_out, SC2);
  not not_30 (not_30_out, SC2);
  not not_31 (not_31_out, SC1);
  not not_32 (not_32_out, SC0);
  not not_33 (not_33_out, OPC1);
  not not_34 (not_34_out, SC2);
  not not_35 (not_35_out, SC2);
  not not_36 (not_36_out, SC2);
  not not_37 (not_37_out, SC1);
  not not_38 (not_38_out, OPC1);
  not not_39 (not_39_out, SC1);
  not not_40 (not_40_out, SC0);
  not not_41 (not_41_out, SC1);
  not not_42 (not_42_out, SC0);
  not not_43 (not_43_out, OPC0);
  not not_44 (not_44_out, SC2);
  and and_1 (C0, not_1_out, not_2_out, not_3_out);
  and and_2 (C1, not_4_out, not_5_out, SC0);
  and and_3 (C2, OPC1, OPC0, SC2, not_6_out, not_7_out);
  and and_4 (and_4_out, not_8_out, not_9_out, SC0);
  and and_5 (and_5_out, not_10_out, SC2, not_11_out, not_12_out);
  and and_6 (and_6_out, not_13_out, not_14_out, SC0);
  and and_7 (and_7_out, not_15_out, SC2, not_16_out, not_17_out);
  and and_8 (and_8_out, OPC1, OPC0, not_18_out, SC0);
  and and_9 (and_9_out, not_19_out, SC1, not_20_out);
  and and_10 (and_10_out, not_21_out, SC2, not_22_out, SC0);
  and and_11 (C6, OPC1, OPC0, SC2, not_23_out, not_24_out);
  and and_12 (C7, not_25_out, SC1, not_26_out);
  and and_13 (and_13_out, not_27_out, not_28_out, SC1, SC0);
  and and_14 (and_14_out, OPC0, not_29_out, SC1, SC0);
  and and_15 (and_15_out, not_30_out, not_31_out, not_32_out);
  and and_16 (and_16_out, not_33_out, not_34_out, SC1, SC0);
  and and_17 (and_17_out, OPC0, not_35_out, SC1, SC0);
  and and_18 (and_18_out, not_36_out, not_37_out, SC0);
  and and_19 (and_19_out, not_38_out, SC2, not_39_out, not_40_out);
  and and_20 (and_20_out, OPC0, SC2, not_41_out, not_42_out);
  and and_21 (C11, OPC1, not_43_out, not_44_out, SC1, SC0);
  or or_1 (C3, and_4_out, and_5_out);
  or or_2 (C4, and_6_out, and_7_out, and_8_out);
  or or_3 (C5, and_9_out, and_10_out);
  or or_4 (C8, and_13_out, and_14_out);
  or or_5 (C9, and_15_out, and_16_out, and_17_out);
  or or_6 (C10, and_18_out, and_19_out, and_20_out);
endmodule

module Control_unit_2 (
  input  OPC3,
  input  OPC2,
  input  OPC1,
  input  OPC0,
  input  SC2,
  input  SC1,
  input  SC0,
  output C12,
  output C13,
  output C14,
  output C15
);

  wire not_1_out, not_2_out, not_3_out, not_4_out, not_5_out, not_6_out, not_7_out, not_8_out;

  not not_1 (not_1_out, OPC1);
  not not_2 (not_2_out, OPC0);
  not not_3 (not_3_out, SC1);
  not not_4 (not_4_out, OPC1);
  not not_5 (not_5_out, SC1);
  not not_6 (not_6_out, SC2);
  not not_7 (not_7_out, OPC0);
  not not_8 (not_8_out, SC2);
  and and_1 (C12, not_1_out, not_2_out, SC2, not_3_out, SC0);
  and and_2 (C13, not_4_out, OPC0, SC2, not_5_out, SC0);
  and and_3 (C14, OPC1, OPC0, not_6_out, SC1, SC0);
  and and_4 (C15, OPC1, not_7_out, not_8_out, SC1, SC0);
endmodule

module Full_Adder (
  input  A,
  input  B,
  input  Cin,
  output Sum,
  output Cout
);

  wire and_1_out, and_2_out, xor_1_out;

  xor xor_1 (xor_1_out, A, B);
  xor xor_2 (Sum, xor_1_out, Cin);
  and and_1 (and_1_out, Cin, xor_1_out);
  and and_2 (and_2_out, B, A);
  or or_1 (Cout, and_1_out, and_2_out);
endmodule

module Adder (
  input  in_1,
  input  [7:0] B,
  input  [7:0] A,
  output [7:0] SUM,
  output Cout
);

  wire full_adder_1_cout, full_adder_2_cout, full_adder_3_cout, full_adder_4_cout, full_adder_5_cout,
       full_adder_6_cout, full_adder_7_cout;

  Full_Adder full_adder_1 (.A(A[0]), .B(B[0]), .Cin(in_1), .Sum(SUM[0]), .Cout(full_adder_1_cout));
  Full_Adder full_adder_2 (.A(A[1]), .B(full_adder_1_cout), .Cin(B[1]), .Sum(SUM[1]), .Cout(full_adder_2_cout));
  Full_Adder full_adder_3 (.A(A[2]), .B(B[2]), .Cin(full_adder_2_cout), .Sum(SUM[2]), .Cout(full_adder_3_cout));
  Full_Adder full_adder_4 (.A(A[3]), .B(B[3]), .Cin(full_adder_3_cout), .Sum(SUM[3]), .Cout(full_adder_4_cout));
  Full_Adder full_adder_5 (.A(A[4]), .B(B[4]), .Cin(full_adder_4_cout), .Sum(SUM[4]), .Cout(full_adder_5_cout));
  Full_Adder full_adder_6 (.A(A[5]), .B(B[5]), .Cin(full_adder_5_cout), .Sum(SUM[5]), .Cout(full_adder_6_cout));
  Full_Adder full_adder_7 (.A(A[6]), .B(B[6]), .Cin(full_adder_6_cout), .Sum(SUM[6]), .Cout(full_adder_7_cout));
  Full_Adder full_adder_8 (.A(A[7]), .B(B[7]), .Cin(full_adder_7_cout), .Sum(SUM[7]), .Cout(Cout));
endmodule

module mini_subtractor (
  input  A,
  input  B,
  input  Bin,
  output Difference,
  output Bout
);

  wire and_1_out, and_2_out, and_3_out, not_1_out, not_2_out, xor_1_out;

  not not_1 (not_1_out, A);
  and and_1 (and_1_out, B, Bin);
  xor xor_1 (xor_1_out, A, B);
  and and_2 (and_2_out, not_1_out, B);
  not not_2 (not_2_out, xor_1_out);
  xor xor_2 (Difference, xor_1_out, Bin);
  and and_3 (and_3_out, not_2_out, Bin);
  or or_1 (Bout, and_3_out, and_1_out, and_2_out);
endmodule

module subtractor (
  input  [7:0] A,
  input  [7:0] B,
  output [7:0] D,
  output Bout
);

  wire mini_subtractor_1_bout, mini_subtractor_2_bout, mini_subtractor_3_bout, mini_subtractor_4_bout,
       mini_subtractor_5_bout, mini_subtractor_6_bout, mini_subtractor_7_bout;

  mini_subtractor mini_subtractor_1 (.A(A[0]), .B(B[0]), .Bin(1'b0), .Difference(D[0]), .Bout(mini_subtractor_1_bout));
  mini_subtractor mini_subtractor_2 (
    .A(A[1]), .B(B[1]), .Bin(mini_subtractor_1_bout), .Difference(D[1]), .Bout(mini_subtractor_2_bout));
  mini_subtractor mini_subtractor_3 (
    .A(A[2]), .B(B[2]), .Bin(mini_subtractor_2_bout), .Difference(D[2]), .Bout(mini_subtractor_3_bout));
  mini_subtractor mini_subtractor_4 (
    .A(A[3]), .B(B[3]), .Bin(mini_subtractor_3_bout), .Difference(D[3]), .Bout(mini_subtractor_4_bout));
  mini_subtractor mini_subtractor_5 (
    .A(A[4]), .B(B[4]), .Bin(mini_subtractor_4_bout), .Difference(D[4]), .Bout(mini_subtractor_5_bout));
  mini_subtractor mini_subtractor_6 (
    .A(A[5]), .B(B[5]), .Bin(mini_subtractor_5_bout), .Difference(D[5]), .Bout(mini_subtractor_6_bout));
  mini_subtractor mini_subtractor_7 (
    .A(A[6]), .B(B[6]), .Bin(mini_subtractor_6_bout), .Difference(D[6]), .Bout(mini_subtractor_7_bout));
  mini_subtractor mini_subtractor_8 (.A(A[7]), .B(B[7]), .Bin(mini_subtractor_7_bout), .Difference(D[7]), .Bout(Bout));
endmodule

module Divider (
  input  Cin,
  input  a,
  input  d,
  input  ck,
  output Cout,
  output S,
  output d_2,
  output k
);

  wire and_1_out, and_2_out, xor_2_out, xor_3_out;

  and and_1 (and_1_out, a, xor_2_out);
  or or_1 (Cout, and_1_out, and_2_out);
  and and_2 (and_2_out, Cin, xor_3_out);
  xor xor_1 (S, Cin, xor_3_out);
  xor xor_2 (xor_2_out, d, ck);
  xor xor_3 (xor_3_out, a, xor_2_out);

  assign d_2 = d;
  assign k = ck;
endmodule

module _8x8Divider (
  input  [7:0] A,
  input  [7:0] B,
  input  k,
  output [7:0] Q
);

  wire divider_1_d_2, divider_1_k, divider_2_cout, divider_2_d_2, divider_2_k, divider_2_s, divider_3_d_2,
       divider_3_k, divider_4_cout, divider_4_d_2, divider_4_k, divider_4_s, divider_5_cout, divider_5_d_2,
       divider_5_k, divider_5_s, divider_6_d_2, divider_6_k, divider_7_cout, divider_7_d_2, divider_7_k,
       divider_7_s, divider_8_cout, divider_8_d_2, divider_8_k, divider_8_s, divider_9_cout, divider_9_d_2,
       divider_9_k, divider_9_s, divider_10_d_2, divider_10_k, divider_11_cout, divider_11_d_2, divider_11_k,
       divider_11_s, divider_12_cout, divider_12_d_2, divider_12_k, divider_12_s, divider_13_cout,
       divider_13_d_2, divider_13_k, divider_13_s, divider_14_cout, divider_14_d_2, divider_14_k,
       divider_14_s, divider_15_d_2, divider_15_k, divider_16_cout, divider_16_d_2, divider_16_k,
       divider_16_s, divider_17_cout, divider_17_d_2, divider_17_k, divider_17_s, divider_18_cout,
       divider_18_d_2, divider_18_k, divider_18_s, divider_19_cout, divider_19_d_2, divider_19_k,
       divider_19_s, divider_20_cout, divider_20_d_2, divider_20_k, divider_20_s, divider_21_d_2,
       divider_21_k, divider_22_cout, divider_22_d_2, divider_22_k, divider_22_s, divider_23_cout,
       divider_23_d_2, divider_23_k, divider_23_s, divider_24_cout, divider_24_d_2, divider_24_k,
       divider_24_s, divider_25_cout, divider_25_d_2, divider_25_k, divider_25_s, divider_26_cout,
       divider_26_d_2, divider_26_k, divider_26_s, divider_27_cout, divider_27_d_2, divider_27_k,
       divider_27_s, divider_28_cout, divider_28_d_2, divider_28_k, divider_28_s, divider_29_d_2,
       divider_29_k, divider_30_cout, divider_30_d_2, divider_30_k, divider_30_s, divider_31_k,
       divider_32_cout, divider_32_d_2, divider_32_k, divider_32_s, divider_33_cout, divider_33_d_2,
       divider_33_k, divider_33_s, divider_34_cout, divider_34_d_2, divider_34_k, divider_34_s,
       divider_35_cout, divider_35_d_2, divider_35_k, divider_35_s, divider_36_cout, divider_36_d_2,
       divider_36_k, divider_36_s, divider_37_cout, divider_37_d_2, divider_37_k, divider_37_s,
       divider_38_cout, divider_38_d_2, divider_38_k, divider_38_s, divider_39_cout, divider_39_k,
       divider_40_cout, divider_40_d_2, divider_40_k, divider_40_s, divider_41_cout, divider_41_d_2,
       divider_41_k, divider_41_s, divider_42_cout, divider_42_d_2, divider_42_k, divider_42_s,
       divider_43_cout, divider_43_d_2, divider_43_k, divider_43_s, divider_44_cout, divider_44_d_2,
       divider_44_k, divider_44_s, divider_45_cout, divider_45_d_2, divider_45_k, divider_45_s,
       divider_46_cout, divider_46_d_2, divider_46_k, divider_46_s, divider_47_cout, divider_47_d_2,
       divider_47_k, divider_47_s, divider_48_cout, divider_48_d_2, divider_48_k, divider_48_s,
       divider_49_cout, divider_49_d_2, divider_49_k, divider_49_s, divider_50_cout, divider_50_k,
       divider_51_cout, divider_51_d_2, divider_51_k, divider_51_s, divider_52_cout, divider_52_d_2,
       divider_52_k, divider_52_s, divider_53_cout, divider_53_d_2, divider_53_k, divider_53_s,
       divider_54_cout, divider_54_d_2, divider_54_k, divider_54_s, divider_55_cout, divider_55_d_2,
       divider_55_k, divider_55_s, divider_56_cout, divider_56_d_2, divider_56_k, divider_56_s,
       divider_57_cout, divider_57_k, divider_58_cout, divider_58_d_2, divider_58_k, divider_58_s,
       divider_59_cout, divider_59_d_2, divider_59_k, divider_59_s, divider_60_cout, divider_60_d_2,
       divider_60_k, divider_60_s, divider_61_cout, divider_61_d_2, divider_61_k, divider_61_s,
       divider_62_cout, divider_62_k, divider_63_cout, divider_63_d_2, divider_63_k, divider_63_s,
       divider_64_cout, divider_64_d_2, divider_64_k, divider_64_s, divider_65_cout, divider_65_d_2,
       divider_65_k, divider_65_s, divider_66_cout, divider_66_k, divider_67_cout, divider_67_d_2,
       divider_67_k, divider_67_s, divider_68_cout, divider_68_d_2, divider_68_k, divider_68_s,
       divider_69_cout, divider_69_k, divider_70_cout, divider_70_d_2, divider_70_k, divider_70_s,
       divider_71_cout, divider_71_k, divider_72_cout, divider_72_k;

  Divider divider_1 (
    .Cin(divider_2_cout), .a(1'b0), .d(1'b0), .ck(k), .Cout(Q[7]), .d_2(divider_1_d_2), .k(divider_1_k));  // open: S
  Divider divider_2 (
    .Cin(divider_4_cout), .a(1'b0), .d(B[7]), .ck(divider_1_k), .Cout(divider_2_cout), .S(divider_2_s),
    .d_2(divider_2_d_2), .k(divider_2_k));
  Divider divider_3 (
    .Cin(divider_5_cout), .a(divider_2_s), .d(divider_1_d_2), .ck(Q[7]), .Cout(Q[6]), .d_2(divider_3_d_2),
    .k(divider_3_k));  // open: S
  Divider divider_4 (
    .Cin(divider_7_cout), .a(1'b0), .d(B[6]), .ck(divider_2_k), .Cout(divider_4_cout), .S(divider_4_s),
    .d_2(divider_4_d_2), .k(divider_4_k));
  Divider divider_5 (
    .Cin(divider_8_cout), .a(divider_4_s), .d(divider_2_d_2), .ck(divider_3_k), .Cout(divider_5_cout),
    .S(divider_5_s), .d_2(divider_5_d_2), .k(divider_5_k));
  Divider divider_6 (
    .Cin(divider_9_cout), .a(divider_5_s), .d(divider_3_d_2), .ck(Q[6]), .Cout(Q[5]), .d_2(divider_6_d_2),
    .k(divider_6_k));  // open: S
  Divider divider_7 (
    .Cin(divider_11_cout), .a(1'b0), .d(B[5]), .ck(divider_4_k), .Cout(divider_7_cout), .S(divider_7_s),
    .d_2(divider_7_d_2), .k(divider_7_k));
  Divider divider_8 (
    .Cin(divider_12_cout), .a(divider_7_s), .d(divider_4_d_2), .ck(divider_5_k), .Cout(divider_8_cout),
    .S(divider_8_s), .d_2(divider_8_d_2), .k(divider_8_k));
  Divider divider_9 (
    .Cin(divider_13_cout), .a(divider_8_s), .d(divider_5_d_2), .ck(divider_6_k), .Cout(divider_9_cout),
    .S(divider_9_s), .d_2(divider_9_d_2), .k(divider_9_k));
  Divider divider_10 (
    .Cin(divider_14_cout), .a(divider_9_s), .d(divider_6_d_2), .ck(Q[5]), .Cout(Q[4]), .d_2(divider_10_d_2),
    .k(divider_10_k));  // open: S
  Divider divider_11 (
    .Cin(divider_16_cout), .a(1'b0), .d(B[4]), .ck(divider_7_k), .Cout(divider_11_cout), .S(divider_11_s),
    .d_2(divider_11_d_2), .k(divider_11_k));
  Divider divider_12 (
    .Cin(divider_17_cout), .a(divider_11_s), .d(divider_7_d_2), .ck(divider_8_k), .Cout(divider_12_cout),
    .S(divider_12_s), .d_2(divider_12_d_2), .k(divider_12_k));
  Divider divider_13 (
    .Cin(divider_18_cout), .a(divider_12_s), .d(divider_8_d_2), .ck(divider_9_k), .Cout(divider_13_cout),
    .S(divider_13_s), .d_2(divider_13_d_2), .k(divider_13_k));
  Divider divider_14 (
    .Cin(divider_19_cout), .a(divider_13_s), .d(divider_9_d_2), .ck(divider_10_k), .Cout(divider_14_cout),
    .S(divider_14_s), .d_2(divider_14_d_2), .k(divider_14_k));
  Divider divider_15 (
    .Cin(divider_20_cout), .a(divider_14_s), .d(divider_10_d_2), .ck(Q[4]), .Cout(Q[3]),
    .d_2(divider_15_d_2), .k(divider_15_k));  // open: S
  Divider divider_16 (
    .Cin(divider_22_cout), .a(1'b0), .d(B[3]), .ck(divider_11_k), .Cout(divider_16_cout), .S(divider_16_s),
    .d_2(divider_16_d_2), .k(divider_16_k));
  Divider divider_17 (
    .Cin(divider_23_cout), .a(divider_16_s), .d(divider_11_d_2), .ck(divider_12_k), .Cout(divider_17_cout),
    .S(divider_17_s), .d_2(divider_17_d_2), .k(divider_17_k));
  Divider divider_18 (
    .Cin(divider_24_cout), .a(divider_17_s), .d(divider_12_d_2), .ck(divider_13_k), .Cout(divider_18_cout),
    .S(divider_18_s), .d_2(divider_18_d_2), .k(divider_18_k));
  Divider divider_19 (
    .Cin(divider_25_cout), .a(divider_18_s), .d(divider_13_d_2), .ck(divider_14_k), .Cout(divider_19_cout),
    .S(divider_19_s), .d_2(divider_19_d_2), .k(divider_19_k));
  Divider divider_20 (
    .Cin(divider_27_cout), .a(divider_19_s), .d(divider_14_d_2), .ck(divider_15_k), .Cout(divider_20_cout),
    .S(divider_20_s), .d_2(divider_20_d_2), .k(divider_20_k));
  Divider divider_21 (
    .Cin(divider_28_cout), .a(divider_20_s), .d(divider_15_d_2), .ck(Q[3]), .Cout(Q[2]),
    .d_2(divider_21_d_2), .k(divider_21_k));  // open: S
  Divider divider_22 (
    .Cin(divider_32_cout), .a(1'b0), .d(B[2]), .ck(divider_16_k), .Cout(divider_22_cout), .S(divider_22_s),
    .d_2(divider_22_d_2), .k(divider_22_k));
  Divider divider_23 (
    .Cin(divider_33_cout), .a(divider_22_s), .d(divider_16_d_2), .ck(divider_17_k), .Cout(divider_23_cout),
    .S(divider_23_s), .d_2(divider_23_d_2), .k(divider_23_k));
  Divider divider_24 (
    .Cin(divider_34_cout), .a(divider_23_s), .d(divider_17_d_2), .ck(divider_18_k), .Cout(divider_24_cout),
    .S(divider_24_s), .d_2(divider_24_d_2), .k(divider_24_k));
  Divider divider_25 (
    .Cin(divider_35_cout), .a(divider_24_s), .d(divider_18_d_2), .ck(divider_19_k), .Cout(divider_25_cout),
    .S(divider_25_s), .d_2(divider_25_d_2), .k(divider_25_k));
  Divider divider_26 (
    .Cin(divider_48_cout), .a(divider_35_s), .d(divider_25_d_2), .ck(divider_27_k), .Cout(divider_26_cout),
    .S(divider_26_s), .d_2(divider_26_d_2), .k(divider_26_k));
  Divider divider_27 (
    .Cin(divider_26_cout), .a(divider_25_s), .d(divider_19_d_2), .ck(divider_20_k), .Cout(divider_27_cout),
    .S(divider_27_s), .d_2(divider_27_d_2), .k(divider_27_k));
  Divider divider_28 (
    .Cin(divider_37_cout), .a(divider_27_s), .d(divider_20_d_2), .ck(divider_21_k), .Cout(divider_28_cout),
    .S(divider_28_s), .d_2(divider_28_d_2), .k(divider_28_k));
  Divider divider_29 (
    .Cin(divider_30_cout), .a(divider_28_s), .d(divider_21_d_2), .ck(Q[2]), .Cout(Q[1]),
    .d_2(divider_29_d_2), .k(divider_29_k));  // open: S
  Divider divider_30 (
    .Cin(divider_38_cout), .a(divider_37_s), .d(divider_28_d_2), .ck(divider_29_k), .Cout(divider_30_cout),
    .S(divider_30_s), .d_2(divider_30_d_2), .k(divider_30_k));
  Divider divider_31 (
    .Cin(divider_39_cout), .a(divider_30_s), .d(divider_29_d_2), .ck(Q[1]), .Cout(Q[0]), .k(divider_31_k));  // open: S, d_2
  Divider divider_32 (
    .Cin(divider_40_cout), .a(1'b0), .d(B[1]), .ck(divider_22_k), .Cout(divider_32_cout), .S(divider_32_s),
    .d_2(divider_32_d_2), .k(divider_32_k));
  Divider divider_33 (
    .Cin(divider_42_cout), .a(divider_32_s), .d(divider_22_d_2), .ck(divider_23_k), .Cout(divider_33_cout),
    .S(divider_33_s), .d_2(divider_33_d_2), .k(divider_33_k));
  Divider divider_34 (
    .Cin(divider_43_cout), .a(divider_33_s), .d(divider_23_d_2), .ck(divider_24_k), .Cout(divider_34_cout),
    .S(divider_34_s), .d_2(divider_34_d_2), .k(divider_34_k));
  Divider divider_35 (
    .Cin(divider_46_cout), .a(divider_34_s), .d(divider_24_d_2), .ck(divider_25_k), .Cout(divider_35_cout),
    .S(divider_35_s), .d_2(divider_35_d_2), .k(divider_35_k));
  Divider divider_36 (
    .Cin(divider_54_cout), .a(divider_48_s), .d(divider_26_d_2), .ck(divider_37_k), .Cout(divider_36_cout),
    .S(divider_36_s), .d_2(divider_36_d_2), .k(divider_36_k));
  Divider divider_37 (
    .Cin(divider_36_cout), .a(divider_26_s), .d(divider_27_d_2), .ck(divider_28_k), .Cout(divider_37_cout),
    .S(divider_37_s), .d_2(divider_37_d_2), .k(divider_37_k));
  Divider divider_38 (
    .Cin(divider_49_cout), .a(divider_36_s), .d(divider_37_d_2), .ck(divider_30_k), .Cout(divider_38_cout),
    .S(divider_38_s), .d_2(divider_38_d_2), .k(divider_38_k));
  Divider divider_39 (
    .Cin(divider_50_cout), .a(divider_38_s), .d(divider_30_d_2), .ck(divider_31_k), .Cout(divider_39_cout),
    .k(divider_39_k));  // open: S, d_2
  Divider divider_40 (
    .Cin(divider_40_k), .a(A[7]), .d(B[0]), .ck(divider_32_k), .Cout(divider_40_cout), .S(divider_40_s),
    .d_2(divider_40_d_2), .k(divider_40_k));
  Divider divider_41 (
    .Cin(divider_41_k), .a(A[6]), .d(divider_40_d_2), .ck(divider_42_k), .Cout(divider_41_cout),
    .S(divider_41_s), .d_2(divider_41_d_2), .k(divider_41_k));
  Divider divider_42 (
    .Cin(divider_41_cout), .a(divider_40_s), .d(divider_32_d_2), .ck(divider_33_k), .Cout(divider_42_cout),
    .S(divider_42_s), .d_2(divider_42_d_2), .k(divider_42_k));
  Divider divider_43 (
    .Cin(divider_44_cout), .a(divider_42_s), .d(divider_33_d_2), .ck(divider_34_k), .Cout(divider_43_cout),
    .S(divider_43_s), .d_2(divider_43_d_2), .k(divider_43_k));
  Divider divider_44 (
    .Cin(divider_51_cout), .a(divider_41_s), .d(divider_42_d_2), .ck(divider_43_k), .Cout(divider_44_cout),
    .S(divider_44_s), .d_2(divider_44_d_2), .k(divider_44_k));
  Divider divider_45 (
    .Cin(divider_52_cout), .a(divider_44_s), .d(divider_43_d_2), .ck(divider_46_k), .Cout(divider_45_cout),
    .S(divider_45_s), .d_2(divider_45_d_2), .k(divider_45_k));
  Divider divider_46 (
    .Cin(divider_45_cout), .a(divider_43_s), .d(divider_34_d_2), .ck(divider_35_k), .Cout(divider_46_cout),
    .S(divider_46_s), .d_2(divider_46_d_2), .k(divider_46_k));
  Divider divider_47 (
    .Cin(divider_53_cout), .a(divider_45_s), .d(divider_46_d_2), .ck(divider_48_k), .Cout(divider_47_cout),
    .S(divider_47_s), .d_2(divider_47_d_2), .k(divider_47_k));
  Divider divider_48 (
    .Cin(divider_47_cout), .a(divider_46_s), .d(divider_35_d_2), .ck(divider_26_k), .Cout(divider_48_cout),
    .S(divider_48_s), .d_2(divider_48_d_2), .k(divider_48_k));
  Divider divider_49 (
    .Cin(divider_56_cout), .a(divider_54_s), .d(divider_36_d_2), .ck(divider_38_k), .Cout(divider_49_cout),
    .S(divider_49_s), .d_2(divider_49_d_2), .k(divider_49_k));
  Divider divider_50 (
    .Cin(divider_57_cout), .a(divider_49_s), .d(divider_38_d_2), .ck(divider_39_k), .Cout(divider_50_cout),
    .k(divider_50_k));  // open: S, d_2
  Divider divider_51 (
    .Cin(divider_51_k), .a(A[5]), .d(divider_41_d_2), .ck(divider_44_k), .Cout(divider_51_cout),
    .S(divider_51_s), .d_2(divider_51_d_2), .k(divider_51_k));
  Divider divider_52 (
    .Cin(divider_58_cout), .a(divider_51_s), .d(divider_44_d_2), .ck(divider_45_k), .Cout(divider_52_cout),
    .S(divider_52_s), .d_2(divider_52_d_2), .k(divider_52_k));
  Divider divider_53 (
    .Cin(divider_59_cout), .a(divider_52_s), .d(divider_45_d_2), .ck(divider_47_k), .Cout(divider_53_cout),
    .S(divider_53_s), .d_2(divider_53_d_2), .k(divider_53_k));
  Divider divider_54 (
    .Cin(divider_55_cout), .a(divider_47_s), .d(divider_48_d_2), .ck(divider_36_k), .Cout(divider_54_cout),
    .S(divider_54_s), .d_2(divider_54_d_2), .k(divider_54_k));
  Divider divider_55 (
    .Cin(divider_60_cout), .a(divider_53_s), .d(divider_47_d_2), .ck(divider_54_k), .Cout(divider_55_cout),
    .S(divider_55_s), .d_2(divider_55_d_2), .k(divider_55_k));
  Divider divider_56 (
    .Cin(divider_61_cout), .a(divider_55_s), .d(divider_54_d_2), .ck(divider_49_k), .Cout(divider_56_cout),
    .S(divider_56_s), .d_2(divider_56_d_2), .k(divider_56_k));
  Divider divider_57 (
    .Cin(divider_62_cout), .a(divider_56_s), .d(divider_49_d_2), .ck(divider_50_k), .Cout(divider_57_cout),
    .k(divider_57_k));  // open: S, d_2
  Divider divider_58 (
    .Cin(divider_58_k), .a(A[4]), .d(divider_51_d_2), .ck(divider_52_k), .Cout(divider_58_cout),
    .S(divider_58_s), .d_2(divider_58_d_2), .k(divider_58_k));
  Divider divider_59 (
    .Cin(divider_63_cout), .a(divider_58_s), .d(divider_52_d_2), .ck(divider_53_k), .Cout(divider_59_cout),
    .S(divider_59_s), .d_2(divider_59_d_2), .k(divider_59_k));
  Divider divider_60 (
    .Cin(divider_64_cout), .a(divider_59_s), .d(divider_53_d_2), .ck(divider_55_k), .Cout(divider_60_cout),
    .S(divider_60_s), .d_2(divider_60_d_2), .k(divider_60_k));
  Divider divider_61 (
    .Cin(divider_65_cout), .a(divider_60_s), .d(divider_55_d_2), .ck(divider_56_k), .Cout(divider_61_cout),
    .S(divider_61_s), .d_2(divider_61_d_2), .k(divider_61_k));
  Divider divider_62 (
    .Cin(divider_66_cout), .a(divider_61_s), .d(divider_56_d_2), .ck(divider_57_k), .Cout(divider_62_cout),
    .k(divider_62_k));  // open: S, d_2
  Divider divider_63 (
    .Cin(divider_63_k), .a(A[3]), .d(divider_58_d_2), .ck(divider_59_k), .Cout(divider_63_cout),
    .S(divider_63_s), .d_2(divider_63_d_2), .k(divider_63_k));
  Divider divider_64 (
    .Cin(divider_67_cout), .a(divider_63_s), .d(divider_59_d_2), .ck(divider_60_k), .Cout(divider_64_cout),
    .S(divider_64_s), .d_2(divider_64_d_2), .k(divider_64_k));
  Divider divider_65 (
    .Cin(divider_68_cout), .a(divider_64_s), .d(divider_60_d_2), .ck(divider_61_k), .Cout(divider_65_cout),
    .S(divider_65_s), .d_2(divider_65_d_2), .k(divider_65_k));
  Divider divider_66 (
    .Cin(divider_69_cout), .a(divider_65_s), .d(divider_61_d_2), .ck(divider_62_k), .Cout(divider_66_cout),
    .k(divider_66_k));  // open: S, d_2
  Divider divider_67 (
    .Cin(divider_67_k), .a(A[2]), .d(divider_63_d_2), .ck(divider_64_k), .Cout(divider_67_cout),
    .S(divider_67_s), .d_2(divider_67_d_2), .k(divider_67_k));
  Divider divider_68 (
    .Cin(divider_70_cout), .a(divider_67_s), .d(divider_64_d_2), .ck(divider_65_k), .Cout(divider_68_cout),
    .S(divider_68_s), .d_2(divider_68_d_2), .k(divider_68_k));
  Divider divider_69 (
    .Cin(divider_71_cout), .a(divider_68_s), .d(divider_65_d_2), .ck(divider_66_k), .Cout(divider_69_cout),
    .k(divider_69_k));  // open: S, d_2
  Divider divider_70 (
    .Cin(divider_70_k), .a(A[1]), .d(divider_67_d_2), .ck(divider_68_k), .Cout(divider_70_cout),
    .S(divider_70_s), .d_2(divider_70_d_2), .k(divider_70_k));
  Divider divider_71 (
    .Cin(divider_72_cout), .a(divider_70_s), .d(divider_68_d_2), .ck(divider_69_k), .Cout(divider_71_cout),
    .k(divider_71_k));  // open: S, d_2
  Divider divider_72 (
    .Cin(divider_72_k), .a(A[0]), .d(divider_70_d_2), .ck(divider_71_k), .Cout(divider_72_cout),
    .k(divider_72_k));  // open: S, d_2
endmodule

module _8x8Multipier (
  input  [7:0] A,
  input  [7:0] B,
  input  in_3,
  input  in_4,
  input  in_5,
  input  in_6,
  input  in_7,
  input  in_8,
  input  in_9,
  input  in_10,
  output [15:0] out_11
);

  wire and_1_out, and_2_out, and_3_out, and_4_out, and_5_out, and_6_out, and_7_out, and_8_out, and_9_out,
       and_10_out, and_11_out, and_12_out, and_13_out, and_14_out, and_15_out, and_16_out, and_17_out,
       and_18_out, and_19_out, and_20_out, and_21_out, and_22_out, and_23_out, and_24_out, and_25_out,
       and_26_out, and_27_out, and_28_out, and_29_out, and_30_out, and_31_out, and_32_out, and_33_out,
       and_34_out, and_35_out, and_36_out, and_37_out, and_38_out, and_39_out, and_40_out, and_41_out,
       and_42_out, and_43_out, and_44_out, and_45_out, and_46_out, and_47_out, and_48_out, and_49_out,
       and_50_out, and_51_out, and_52_out, and_53_out, and_54_out, and_55_out, and_56_out, and_57_out,
       and_58_out, and_59_out, and_60_out, and_61_out, and_62_out, and_63_out, full_adder_2_cout,
       full_adder_2_sum, full_adder_3_cout, full_adder_4_cout, full_adder_4_sum, full_adder_5_cout,
       full_adder_5_sum, full_adder_6_cout, full_adder_6_sum, full_adder_7_cout, full_adder_7_sum,
       full_adder_8_cout, full_adder_9_cout, full_adder_9_sum, full_adder_10_cout, full_adder_10_sum,
       full_adder_11_cout, full_adder_11_sum, full_adder_12_cout, full_adder_12_sum, full_adder_13_cout,
       full_adder_13_sum, full_adder_14_cout, full_adder_15_cout, full_adder_15_sum, full_adder_16_cout,
       full_adder_16_sum, full_adder_17_cout, full_adder_17_sum, full_adder_18_cout, full_adder_18_sum,
       full_adder_19_cout, full_adder_19_sum, full_adder_20_cout, full_adder_20_sum, full_adder_21_cout,
       full_adder_22_cout, full_adder_22_sum, full_adder_23_cout, full_adder_23_sum, full_adder_24_cout,
       full_adder_24_sum, full_adder_25_cout, full_adder_25_sum, full_adder_26_cout, full_adder_26_sum,
       full_adder_27_cout, full_adder_27_sum, full_adder_28_cout, full_adder_29_cout, full_adder_29_sum,
       full_adder_30_cout, full_adder_30_sum, full_adder_31_cout, full_adder_31_sum, full_adder_32_cout,
       full_adder_32_sum, full_adder_33_cout, full_adder_33_sum, full_adder_34_cout, full_adder_34_sum,
       full_adder_35_cout, full_adder_36_cout, full_adder_36_sum, full_adder_37_cout, full_adder_37_sum,
       full_adder_38_cout, full_adder_38_sum, full_adder_39_cout, full_adder_39_sum, full_adder_40_cout,
       full_adder_41_cout, full_adder_41_sum, full_adder_42_cout, full_adder_42_sum, full_adder_43_cout,
       full_adder_43_sum, full_adder_44_cout, full_adder_44_sum, full_adder_45_cout, full_adder_45_sum,
       full_adder_46_cout, full_adder_47_cout, full_adder_47_sum, full_adder_48_cout, full_adder_48_sum,
       full_adder_49_cout, full_adder_50_cout, full_adder_50_sum, full_adder_51_cout, full_adder_51_sum,
       full_adder_52_cout, full_adder_53_cout, full_adder_54_cout, full_adder_54_sum, full_adder_55_cout,
       full_adder_56_cout;

  and and_1 (and_1_out, A[7], B[7]);
  and and_2 (and_2_out, A[7], B[6]);
  Full_Adder full_adder_1 (
    .A(full_adder_2_cout), .B(and_1_out), .Cin(full_adder_3_cout), .Sum(out_11[14]), .Cout(out_11[15]));
  Full_Adder full_adder_2 (
    .A(full_adder_4_cout), .B(and_2_out), .Cin(full_adder_5_cout), .Sum(full_adder_2_sum),
    .Cout(full_adder_2_cout));
  and and_3 (and_3_out, A[6], B[7]);
  and and_4 (and_4_out, A[7], B[5]);
  and and_5 (and_5_out, A[6], B[6]);
  Full_Adder full_adder_3 (
    .A(full_adder_2_sum), .B(and_3_out), .Cin(full_adder_8_cout), .Sum(out_11[13]), .Cout(full_adder_3_cout));
  and and_6 (and_6_out, A[7], B[4]);
  and and_7 (and_7_out, A[6], B[5]);
  Full_Adder full_adder_4 (
    .A(full_adder_6_cout), .B(and_4_out), .Cin(full_adder_7_cout), .Sum(full_adder_4_sum),
    .Cout(full_adder_4_cout));
  Full_Adder full_adder_5 (
    .A(full_adder_4_sum), .B(and_5_out), .Cin(full_adder_10_cout), .Sum(full_adder_5_sum),
    .Cout(full_adder_5_cout));
  and and_8 (and_8_out, A[5], B[7]);
  and and_9 (and_9_out, A[6], B[4]);
  Full_Adder full_adder_6 (
    .A(full_adder_12_cout), .B(and_6_out), .Cin(full_adder_9_cout), .Sum(full_adder_6_sum),
    .Cout(full_adder_6_cout));
  Full_Adder full_adder_7 (
    .A(full_adder_6_sum), .B(and_7_out), .Cin(full_adder_13_cout), .Sum(full_adder_7_sum),
    .Cout(full_adder_7_cout));
  and and_10 (and_10_out, A[5], B[6]);
  Full_Adder full_adder_8 (
    .A(full_adder_5_sum), .B(and_8_out), .Cin(full_adder_14_cout), .Sum(out_11[12]), .Cout(full_adder_8_cout));
  and and_11 (and_11_out, A[7], B[2]);
  and and_12 (and_12_out, A[7], B[3]);
  Full_Adder full_adder_9 (
    .A(full_adder_12_sum), .B(and_9_out), .Cin(full_adder_17_cout), .Sum(full_adder_9_sum),
    .Cout(full_adder_9_cout));
  and and_13 (and_13_out, A[5], B[5]);
  Full_Adder full_adder_10 (
    .A(full_adder_7_sum), .B(and_10_out), .Cin(full_adder_18_cout), .Sum(full_adder_10_sum),
    .Cout(full_adder_10_cout));
  and and_14 (and_14_out, A[4], B[7]);
  Full_Adder full_adder_11 (
    .A(full_adder_15_cout), .B(and_11_out), .Cin(full_adder_19_cout), .Sum(full_adder_11_sum),
    .Cout(full_adder_11_cout));
  and and_15 (and_15_out, A[6], B[3]);
  Full_Adder full_adder_12 (
    .A(full_adder_11_cout), .B(and_12_out), .Cin(full_adder_16_cout), .Sum(full_adder_12_sum),
    .Cout(full_adder_12_cout));
  and and_16 (and_16_out, A[5], B[4]);
  Full_Adder full_adder_13 (
    .A(full_adder_9_sum), .B(and_13_out), .Cin(full_adder_20_cout), .Sum(full_adder_13_sum),
    .Cout(full_adder_13_cout));
  and and_17 (and_17_out, A[4], B[6]);
  Full_Adder full_adder_14 (
    .A(full_adder_10_sum), .B(and_14_out), .Cin(full_adder_21_cout), .Sum(out_11[11]),
    .Cout(full_adder_14_cout));
  and and_18 (and_18_out, A[7], B[1]);
  Full_Adder full_adder_15 (
    .A(full_adder_22_cout), .B(and_18_out), .Cin(in_3), .Sum(full_adder_15_sum), .Cout(full_adder_15_cout));
  and and_19 (and_19_out, A[6], B[2]);
  Full_Adder full_adder_16 (
    .A(full_adder_11_sum), .B(and_15_out), .Cin(full_adder_23_cout), .Sum(full_adder_16_sum),
    .Cout(full_adder_16_cout));
  Full_Adder full_adder_17 (
    .A(full_adder_16_sum), .B(and_16_out), .Cin(full_adder_24_cout), .Sum(full_adder_17_sum),
    .Cout(full_adder_17_cout));
  and and_20 (and_20_out, A[4], B[5]);
  Full_Adder full_adder_18 (
    .A(full_adder_13_sum), .B(and_17_out), .Cin(full_adder_25_cout), .Sum(full_adder_18_sum),
    .Cout(full_adder_18_cout));
  and and_21 (and_21_out, A[3], B[7]);
  and and_22 (and_22_out, A[6], B[1]);
  Full_Adder full_adder_19 (
    .A(full_adder_15_sum), .B(and_19_out), .Cin(full_adder_26_cout), .Sum(full_adder_19_sum),
    .Cout(full_adder_19_cout));
  and and_23 (and_23_out, A[5], B[3]);
  and and_24 (and_24_out, A[4], B[4]);
  Full_Adder full_adder_20 (
    .A(full_adder_17_sum), .B(and_20_out), .Cin(full_adder_27_cout), .Sum(full_adder_20_sum),
    .Cout(full_adder_20_cout));
  and and_25 (and_25_out, A[3], B[6]);
  Full_Adder full_adder_21 (
    .A(full_adder_18_sum), .B(and_21_out), .Cin(full_adder_28_cout), .Sum(out_11[10]),
    .Cout(full_adder_21_cout));
  and and_26 (and_26_out, A[7], B[0]);
  Full_Adder full_adder_22 (
    .A(and_26_out), .B(and_22_out), .Cin(full_adder_29_cout), .Sum(full_adder_22_sum),
    .Cout(full_adder_22_cout));
  and and_27 (and_27_out, A[5], B[2]);
  Full_Adder full_adder_23 (
    .A(full_adder_19_sum), .B(and_23_out), .Cin(full_adder_30_cout), .Sum(full_adder_23_sum),
    .Cout(full_adder_23_cout));
  Full_Adder full_adder_24 (
    .A(full_adder_23_sum), .B(and_24_out), .Cin(full_adder_31_cout), .Sum(full_adder_24_sum),
    .Cout(full_adder_24_cout));
  and and_28 (and_28_out, A[3], B[5]);
  Full_Adder full_adder_25 (
    .A(full_adder_20_sum), .B(and_25_out), .Cin(full_adder_32_cout), .Sum(full_adder_25_sum),
    .Cout(full_adder_25_cout));
  and and_29 (and_29_out, A[2], B[7]);
  and and_30 (and_30_out, A[5], B[1]);
  and and_31 (and_31_out, A[4], B[2]);
  Full_Adder full_adder_26 (
    .A(full_adder_22_sum), .B(and_27_out), .Cin(full_adder_33_cout), .Sum(full_adder_26_sum),
    .Cout(full_adder_26_cout));
  and and_32 (and_32_out, A[4], B[3]);
  and and_33 (and_33_out, A[3], B[4]);
  Full_Adder full_adder_27 (
    .A(full_adder_24_sum), .B(and_28_out), .Cin(full_adder_34_cout), .Sum(full_adder_27_sum),
    .Cout(full_adder_27_cout));
  and and_34 (and_34_out, A[2], B[6]);
  and and_35 (and_35_out, A[1], B[7]);
  Full_Adder full_adder_28 (
    .A(full_adder_25_sum), .B(and_29_out), .Cin(full_adder_35_cout), .Sum(out_11[9]),
    .Cout(full_adder_28_cout));
  and and_36 (and_36_out, A[6], B[0]);
  Full_Adder full_adder_29 (
    .A(and_36_out), .B(and_30_out), .Cin(full_adder_36_cout), .Sum(full_adder_29_sum),
    .Cout(full_adder_29_cout));
  Full_Adder full_adder_30 (
    .A(full_adder_26_sum), .B(and_32_out), .Cin(full_adder_37_cout), .Sum(full_adder_30_sum),
    .Cout(full_adder_30_cout));
  Full_Adder full_adder_31 (
    .A(full_adder_30_sum), .B(and_33_out), .Cin(full_adder_38_cout), .Sum(full_adder_31_sum),
    .Cout(full_adder_31_cout));
  and and_37 (and_37_out, A[2], B[5]);
  Full_Adder full_adder_32 (
    .A(full_adder_27_sum), .B(and_34_out), .Cin(full_adder_39_cout), .Sum(full_adder_32_sum),
    .Cout(full_adder_32_cout));
  and and_38 (and_38_out, A[4], B[1]);
  Full_Adder full_adder_33 (
    .A(full_adder_29_sum), .B(and_31_out), .Cin(full_adder_41_cout), .Sum(full_adder_33_sum),
    .Cout(full_adder_33_cout));
  and and_39 (and_39_out, A[3], B[3]);
  and and_40 (and_40_out, A[2], B[4]);
  Full_Adder full_adder_34 (
    .A(full_adder_31_sum), .B(and_37_out), .Cin(full_adder_42_cout), .Sum(full_adder_34_sum),
    .Cout(full_adder_34_cout));
  and and_41 (and_41_out, A[1], B[6]);
  and and_42 (and_42_out, A[0], B[7]);
  Full_Adder full_adder_35 (
    .A(full_adder_32_sum), .B(and_35_out), .Cin(full_adder_40_cout), .Sum(out_11[8]),
    .Cout(full_adder_35_cout));
  and and_43 (and_43_out, A[5], B[0]);
  Full_Adder full_adder_36 (
    .A(and_43_out), .B(and_38_out), .Cin(full_adder_43_cout), .Sum(full_adder_36_sum),
    .Cout(full_adder_36_cout));
  and and_44 (and_44_out, A[3], B[2]);
  Full_Adder full_adder_37 (
    .A(full_adder_33_sum), .B(and_39_out), .Cin(full_adder_44_cout), .Sum(full_adder_37_sum),
    .Cout(full_adder_37_cout));
  Full_Adder full_adder_38 (
    .A(full_adder_37_sum), .B(and_40_out), .Cin(full_adder_45_cout), .Sum(full_adder_38_sum),
    .Cout(full_adder_38_cout));
  and and_45 (and_45_out, A[1], B[5]);
  and and_46 (and_46_out, A[0], B[6]);
  Full_Adder full_adder_39 (
    .A(full_adder_34_sum), .B(and_41_out), .Cin(full_adder_46_cout), .Sum(full_adder_39_sum),
    .Cout(full_adder_39_cout));
  Full_Adder full_adder_40 (
    .A(full_adder_39_sum), .B(and_42_out), .Cin(in_10), .Sum(out_11[7]), .Cout(full_adder_40_cout));
  and and_47 (and_47_out, A[3], B[1]);
  Full_Adder full_adder_41 (
    .A(full_adder_36_sum), .B(and_44_out), .Cin(full_adder_47_cout), .Sum(full_adder_41_sum),
    .Cout(full_adder_41_cout));
  and and_48 (and_48_out, A[2], B[3]);
  and and_49 (and_49_out, A[1], B[4]);
  and and_50 (and_50_out, A[0], B[5]);
  Full_Adder full_adder_42 (
    .A(full_adder_38_sum), .B(and_45_out), .Cin(full_adder_49_cout), .Sum(full_adder_42_sum),
    .Cout(full_adder_42_cout));
  and and_51 (and_51_out, A[4], B[0]);
  Full_Adder full_adder_43 (
    .A(and_51_out), .B(and_47_out), .Cin(full_adder_50_cout), .Sum(full_adder_43_sum),
    .Cout(full_adder_43_cout));
  and and_52 (and_52_out, A[2], B[2]);
  and and_53 (and_53_out, A[1], B[3]);
  Full_Adder full_adder_44 (
    .A(full_adder_41_sum), .B(and_48_out), .Cin(full_adder_48_cout), .Sum(full_adder_44_sum),
    .Cout(full_adder_44_cout));
  Full_Adder full_adder_45 (
    .A(full_adder_44_sum), .B(and_49_out), .Cin(full_adder_52_cout), .Sum(full_adder_45_sum),
    .Cout(full_adder_45_cout));
  Full_Adder full_adder_46 (
    .A(full_adder_42_sum), .B(and_46_out), .Cin(in_9), .Sum(out_11[6]), .Cout(full_adder_46_cout));
  and and_54 (and_54_out, A[2], B[1]);
  and and_55 (and_55_out, A[1], B[2]);
  Full_Adder full_adder_47 (
    .A(full_adder_43_sum), .B(and_52_out), .Cin(full_adder_51_cout), .Sum(full_adder_47_sum),
    .Cout(full_adder_47_cout));
  Full_Adder full_adder_48 (
    .A(full_adder_47_sum), .B(and_53_out), .Cin(full_adder_53_cout), .Sum(full_adder_48_sum),
    .Cout(full_adder_48_cout));
  and and_56 (and_56_out, A[0], B[4]);
  Full_Adder full_adder_49 (
    .A(full_adder_45_sum), .B(and_50_out), .Cin(in_8), .Sum(out_11[5]), .Cout(full_adder_49_cout));
  and and_57 (and_57_out, A[3], B[0]);
  and and_58 (and_58_out, A[1], B[1]);
  Full_Adder full_adder_50 (
    .A(and_57_out), .B(and_54_out), .Cin(full_adder_54_cout), .Sum(full_adder_50_sum),
    .Cout(full_adder_50_cout));
  Full_Adder full_adder_51 (
    .A(full_adder_50_sum), .B(and_55_out), .Cin(full_adder_55_cout), .Sum(full_adder_51_sum),
    .Cout(full_adder_51_cout));
  and and_59 (and_59_out, A[0], B[3]);
  Full_Adder full_adder_52 (
    .A(full_adder_48_sum), .B(and_56_out), .Cin(in_7), .Sum(out_11[4]), .Cout(full_adder_52_cout));
  and and_60 (and_60_out, A[0], B[2]);
  Full_Adder full_adder_53 (
    .A(full_adder_51_sum), .B(and_59_out), .Cin(in_6), .Sum(out_11[3]), .Cout(full_adder_53_cout));
  and and_61 (and_61_out, A[2], B[0]);
  Full_Adder full_adder_54 (
    .A(and_61_out), .B(and_58_out), .Cin(full_adder_56_cout), .Sum(full_adder_54_sum),
    .Cout(full_adder_54_cout));
  Full_Adder full_adder_55 (
    .A(full_adder_54_sum), .B(and_60_out), .Cin(in_5), .Sum(out_11[2]), .Cout(full_adder_55_cout));
  and and_62 (and_62_out, A[0], B[1]);
  Full_Adder full_adder_56 (.A(and_63_out), .B(and_62_out), .Cin(in_4), .Sum(out_11[1]), .Cout(full_adder_56_cout));
  and and_63 (and_63_out, A[1], B[0]);
  and and_64 (out_11[0], A[0], B[0]);
endmodule

module _8x3MUX (
  input  [7:0] d0,
  input  [7:0] d1,
  input  [7:0] d2,
  input  [7:0] d3,
  input  [7:0] d4,
  input  [7:0] d5,
  input  [7:0] d6,
  input  [7:0] d7,
  input  [2:0] in_9,
  output [7:0] out
);

  wire [7:0] and_1_out, and_2_out, and_3_out, and_4_out, and_5_out, and_6_out, and_7_out, and_8_out,
       not_1_out, not_2_out, not_3_out;

  assign not_1_out = ~{8{in_9[2]}};  // NOT_Gate not_1, 8 bits wide
  assign not_2_out = ~{8{in_9[1]}};  // NOT_Gate not_2, 8 bits wide
  assign not_3_out = ~{8{in_9[0]}};  // NOT_Gate not_3, 8 bits wide
  assign and_1_out = not_3_out & not_2_out & not_1_out & d0;  // AND_Gate and_1, 8 bits wide
  assign and_2_out = {8{in_9[0]}} & not_2_out & not_1_out & d1;  // AND_Gate and_2, 8 bits wide
  assign and_3_out = not_3_out & {8{in_9[1]}} & not_1_out & d2;  // AND_Gate and_3, 8 bits wide
  assign and_4_out = {8{in_9[0]}} & {8{in_9[1]}} & not_1_out & d3;  // AND_Gate and_4, 8 bits wide
  assign and_5_out = not_3_out & not_2_out & {8{in_9[2]}} & d4;  // AND_Gate and_5, 8 bits wide
  assign and_6_out = {8{in_9[0]}} & not_2_out & {8{in_9[2]}} & d5;  // AND_Gate and_6, 8 bits wide
  assign and_7_out = not_3_out & {8{in_9[1]}} & {8{in_9[2]}} & d6;  // AND_Gate and_7, 8 bits wide
  assign and_8_out = {8{in_9[0]}} & {8{in_9[1]}} & {8{in_9[2]}} & d7;  // AND_Gate and_8, 8 bits wide
  assign out = and_1_out | and_2_out | and_3_out | and_4_out | and_5_out | and_6_out | and_7_out | and_8_out;  // OR_Gate or_1, 8 bits wide
endmodule
